# Fritzing sketch Teste_sinaistransitoeoutrosV0.01 (saved by Fritzing 0.9.4)
breadboards: 2

parts:
  Componente1 = Arduino Uno (Rev3)  # not connected
  RHT1 = Humidity and Temperature Sensor RHT03  # not connected
  7_Segment1 = 7 Segment Display
  7_Segment2 = 7 Segment Display
  7_Segment3 = 7 Segment Display
  7_Segment4 = 7 Segment Display
  S1 = Pushbutton [package="[THT]"]
  LED1 = LED - 5mm [color="Green (570nm)" package="5 mm [THT]"]  # not connected
  LED2 = LED - 5mm [color="Green (570nm)" package="5 mm [THT]"]  # not connected
  LED3 = LED - 5mm [color="Red (633nm)" package="5 mm [THT]"]  # not connected
  LED4 = LED - 5mm [color="Red (633nm)" package="5 mm [THT]"]  # not connected
  LED5 = LED - 5mm [color="Yellow (595nm)" package="5 mm [THT]"]  # not connected

nets:
  N1: 7_Segment1.Segment_G, 7_Segment1.Segment_F
  N2: 7_Segment1.Segment_B, 7_Segment1.Segment_A
  N3: 7_Segment2.Segment_G, 7_Segment2.Segment_F
  N4: 7_Segment2.Segment_B, 7_Segment2.Segment_A
  N5: 7_Segment3.Segment_G, 7_Segment3.Segment_F
  N6: 7_Segment3.Segment_B, 7_Segment3.Segment_A
  N7: 7_Segment4.Segment_G, 7_Segment4.Segment_F
  N8: 7_Segment4.Segment_B, 7_Segment4.Segment_A
  N9: S1.Pin_1, S1.Pin_2
  N10: S1.Pin_3, S1.Pin_4
